// Logisim project ControlUnit.circ as structural Verilog: 1 circuit, main circuit main
module main (
  input  Clock,
  input  go_i,
  input  Ei,
  input  Ej,
  input  Eflgi,
  input  Eflgj,
  input  EgtWht,
  input  EgtRed,
  output Lred,
  output Lwht,
  output Reset,
  output Lt,
  output Lg,
  output Lj,
  output Sj,
  output Lflag,
  output Sred,
  output Swht,
  output SwrAdder,
  output Li,
  output Si,
  output SjiAdder
);

  wire and_1_out, and_2_out, and_3_out, and_4_out, and_5_out, and_6_out, and_7_out, and_8_out,
       decoder_1_out0, decoder_1_out2, decoder_1_out3, decoder_1_out5, decoder_1_out6, decoder_1_out7,
       decoder_1_out8, decoder_1_out9, decoder_1_out11, decoder_1_out13, not_1_out, not_2_out, not_3_out,
       not_4_out, not_5_out, not_6_out, or_1_out, or_2_out, or_3_out, or_4_out, or_5_out, or_6_out, or_7_out;
  wire [3:0] register_4_q;

  or or_1 (or_1_out, decoder_1_out7, decoder_1_out8, decoder_1_out9, Swht, decoder_1_out11, decoder_1_out13);
  and and_1 (and_1_out, decoder_1_out7, Ei);
  and and_2 (and_2_out, decoder_1_out9, Ej);
  or or_2 (or_2_out, and_1_out, and_2_out, decoder_1_out13, decoder_1_out3, Sred, decoder_1_out6, Si);
  and and_3 (and_3_out, go_i, decoder_1_out0);
  or or_3 (or_3_out, decoder_1_out8, and_1_out, and_3_out, and_4_out, decoder_1_out2, or_6_out, and_8_out, or_4_out);
  not not_1 (not_1_out, Ej);
  and and_4 (and_4_out, decoder_1_out3, not_1_out, not_2_out);
  Register #(.width(1)) register_1 (.D(or_1_out), .Q(register_4_q[3]), .clk(Clock));  // open: en, clr
  not not_2 (not_2_out, EgtRed);
  Decoder #(.select(4), .enable("false")) decoder_1 (
    .out0(decoder_1_out0), .out1(Lg), .out2(decoder_1_out2), .out3(decoder_1_out3), .out4(Sred),
    .out5(decoder_1_out5), .out6(decoder_1_out6), .out7(decoder_1_out7), .out8(decoder_1_out8),
    .out9(decoder_1_out9), .out10(Swht), .out11(decoder_1_out11), .out12(Si), .out13(decoder_1_out13),
    .sel(register_4_q));  // open: out14, out15
  or or_4 (or_4_out, Swht, decoder_1_out11, Si, decoder_1_out13);
  Register #(.width(1)) register_2 (.D(or_2_out), .Q(register_4_q[2]), .clk(Clock));  // open: en, clr
  Register #(.width(1)) register_3 (.D(or_5_out), .Q(register_4_q[1]), .clk(Clock));  // open: en, clr
  Register #(.width(1)) register_4 (.D(or_3_out), .Q(register_4_q[0]), .clk(Clock));  // open: en, clr
  or or_5 (or_5_out, Lg, decoder_1_out2, and_5_out, decoder_1_out5, decoder_1_out6, Si, Swht, and_6_out, and_8_out);
  or or_6 (or_6_out, Sred, decoder_1_out5, decoder_1_out6);
  and and_5 (and_5_out, decoder_1_out3, Ej);
  not not_3 (not_3_out, Ej);
  and and_6 (and_6_out, decoder_1_out9, not_3_out, EgtWht, Eflgj, Eflgi);
  not not_4 (not_4_out, Eflgi);
  not not_5 (not_5_out, Eflgj);
  or or_7 (or_7_out, not_4_out, not_5_out, not_6_out);
  or or_8 (Li, decoder_1_out6, Si);
  and and_7 (and_7_out, decoder_1_out9, not_3_out);
  not not_6 (not_6_out, EgtWht);
  and and_8 (and_8_out, or_7_out, and_7_out);
  or or_9 (Lred, Sred, Lg);
  or or_10 (Lwht, Lg, Swht);
  or or_11 (Lflag, Sred, Swht);
  or or_12 (Lj, decoder_1_out2, decoder_1_out5, decoder_1_out8, decoder_1_out11);
  or or_13 (Sj, decoder_1_out5, decoder_1_out11);

  assign Lt = Lg;
  assign Reset = Lg;
  assign SjiAdder = Si;
  assign SwrAdder = Sred;

  // Notes on the sheet:
  //   S7
  //   S9
  //   S8
  //   S13
  //   S10
  //   S11
  //   Eflj'+Eflgi'+EgtWht'
  //   S9.Ej'
endmodule
