// Logisim project Datapath.circ as structural Verilog: 1 circuit, main circuit main
module main (
  input  Clock,
  input  Lg,
  input  [2:0] in0,
  input  [2:0] in1,
  input  [2:0] in2,
  input  [2:0] in3,
  input  Lt,
  input  Sj,
  input  Si,
  input  Swht,
  input  Sred,
  input  Lj,
  input  Li,
  input  Lwht,
  input  Lred,
  input  SwrAdder,
  input  SjiAdder,
  input  Reset,
  input  Lflag,
  output EgtRed,
  output EgtWht,
  output [2:0] RED,
  output [2:0] WHITE,
  output Ej,
  output Ei,
  output Eflgi,
  output Eflgj
);

  wire demultiplexer_1_out0, demultiplexer_1_out1, demultiplexer_1_out2, demultiplexer_1_out3,
       multiplexer_6_out, multiplexer_7_out, register_10_q, register_11_q, register_12_q, register_13_q;
  wire [2:0] adder_1_out, adder_2_out, multiplexer_1_out, multiplexer_2_out, multiplexer_3_out,
       multiplexer_4_out, multiplexer_5_out, multiplexer_8_out, multiplexer_9_out, multiplexer_10_out,
       multiplexer_11_out, multiplexer_12_out, register_1_q, register_2_q, register_3_q, register_4_q,
       register_5_q, register_6_q, register_7_q, register_8_q, register_9_q, register_14_q;
  wire [11:0] random_1_out;

  Random #(.width(12)) random_1 (.clk(Clock), .out(random_1_out));  // open: next, clr
  Multiplexer #(.width(3), .enable("false")) multiplexer_1 (
    .in0(3'b000), .in1(adder_1_out), .out(multiplexer_1_out), .sel(Sj));
  Demultiplexer #(.select(2), .enable("false")) demultiplexer_1 (
    .out0(demultiplexer_1_out0), .out1(demultiplexer_1_out1), .out2(demultiplexer_1_out2),
    .out3(demultiplexer_1_out3), .in(Lflag), .sel(register_1_q[1:0]));
  Register #(.width(3)) register_1 (.D(multiplexer_1_out), .en(Lj), .Q(register_1_q), .clk(Clock));  // open: clr
  Register #(.width(3)) register_2 (.D(in0), .en(Lg), .Q(register_2_q), .clk(Clock));  // open: clr
  Register #(.width(3)) register_3 (.D(in1), .en(Lg), .Q(register_3_q), .clk(Clock));  // open: clr
  Register #(.width(3)) register_4 (.D(in2), .en(Lg), .Q(register_4_q), .clk(Clock));  // open: clr
  Register #(.width(3)) register_5 (.D(in3), .en(Lg), .Q(register_5_q), .clk(Clock));  // open: clr
  Register #(.width(3)) register_6 (.D(random_1_out[2:0]), .en(Lt), .Q(register_6_q), .clk(Clock));  // open: clr
  Register #(.width(3)) register_7 (.D(random_1_out[5:3]), .en(Lt), .Q(register_7_q), .clk(Clock));  // open: clr
  Register #(.width(3)) register_8 (.D(random_1_out[8:6]), .en(Lt), .Q(register_8_q), .clk(Clock));  // open: clr
  Register #(.width(3)) register_9 (.D(random_1_out[11:9]), .en(Lt), .Q(register_9_q), .clk(Clock));  // open: clr
  Comparator #(.width(3)) comparator_1 (.a(register_1_q), .b(3'b100), .eq(Ej));  // open: gt, lt
  Register #(.width(1)) register_10 (.D(1'b1), .en(demultiplexer_1_out0), .Q(register_10_q), .clk(Clock), .clr(Reset));
  Register #(.width(1)) register_11 (.D(1'b1), .en(demultiplexer_1_out1), .Q(register_11_q), .clk(Clock), .clr(Reset));
  Register #(.width(1)) register_12 (.D(1'b1), .en(demultiplexer_1_out2), .Q(register_12_q), .clk(Clock), .clr(Reset));
  Register #(.width(1)) register_13 (.D(1'b1), .en(demultiplexer_1_out3), .Q(register_13_q), .clk(Clock), .clr(Reset));
  Multiplexer #(.select(2), .width(3), .enable("false")) multiplexer_2 (
    .in0(register_2_q), .in1(register_3_q), .in2(register_4_q), .in3(register_5_q), .out(multiplexer_2_out),
    .sel(register_1_q[1:0]));
  Multiplexer #(.select(2), .width(3), .enable("false")) multiplexer_3 (
    .in0(register_6_q), .in1(register_7_q), .in2(register_8_q), .in3(register_9_q), .out(multiplexer_3_out),
    .sel(register_1_q[1:0]));
  Multiplexer #(.width(3), .enable("false")) multiplexer_4 (
    .in0(register_1_q), .in1(register_14_q), .out(multiplexer_4_out), .sel(SjiAdder));
  Adder #(.width(3)) adder_1 (.a(3'b001), .b(multiplexer_4_out), .out(adder_1_out));  // open: cin, cout
  Comparator #(.width(3)) comparator_2 (.a(multiplexer_2_out), .b(multiplexer_3_out), .eq(EgtRed));  // open: gt, lt
  Multiplexer #(.width(3), .enable("false")) multiplexer_5 (
    .in0(3'b000), .in1(adder_1_out), .out(multiplexer_5_out), .sel(Si));
  Register #(.width(3)) register_14 (.D(multiplexer_5_out), .en(Li), .Q(register_14_q), .clk(Clock));  // open: clr
  Multiplexer #(.select(2), .enable("false")) multiplexer_6 (
    .in0(register_10_q), .in1(register_11_q), .in2(register_12_q), .in3(register_13_q),
    .out(multiplexer_6_out), .sel(register_14_q[1:0]));
  Multiplexer #(.select(2), .enable("false")) multiplexer_7 (
    .in0(register_10_q), .in1(register_11_q), .in2(register_12_q), .in3(register_13_q),
    .out(multiplexer_7_out), .sel(register_1_q[1:0]));
  Comparator #(.width(3)) comparator_3 (.a(register_14_q), .b(3'b100), .eq(Ei));  // open: gt, lt
  Multiplexer #(.select(2), .width(3), .enable("false")) multiplexer_8 (
    .in0(register_2_q), .in1(register_3_q), .in2(register_4_q), .in3(register_5_q), .out(multiplexer_8_out),
    .sel(register_1_q[1:0]));
  Multiplexer #(.select(2), .width(3), .enable("false")) multiplexer_9 (
    .in0(register_6_q), .in1(register_7_q), .in2(register_8_q), .in3(register_9_q), .out(multiplexer_9_out),
    .sel(register_14_q[1:0]));
  nor nor_1 (Eflgi, 1'b0, multiplexer_6_out);
  nor nor_2 (Eflgj, 1'b0, multiplexer_7_out);
  Comparator #(.width(3)) comparator_4 (.a(multiplexer_8_out), .b(multiplexer_9_out), .eq(EgtWht));  // open: gt, lt
  Multiplexer #(.width(3), .enable("false")) multiplexer_10 (
    .in0(3'b000), .in1(adder_2_out), .out(multiplexer_10_out), .sel(Swht));
  Register #(.width(3)) register_15 (.D(multiplexer_10_out), .en(Lwht), .Q(WHITE), .clk(Clock));  // open: clr
  Multiplexer #(.width(3), .enable("false")) multiplexer_11 (
    .in0(WHITE), .in1(RED), .out(multiplexer_11_out), .sel(SwrAdder));
  Adder #(.width(3)) adder_2 (.a(3'b001), .b(multiplexer_11_out), .out(adder_2_out));  // open: cin, cout
  Multiplexer #(.width(3), .enable("false")) multiplexer_12 (
    .in0(3'b000), .in1(adder_2_out), .out(multiplexer_12_out), .sel(Sred));
  Register #(.width(3)) register_16 (.D(multiplexer_12_out), .en(Lred), .Q(RED), .clk(Clock));  // open: clr

  // Notes on the sheet:
  //   j+1
  //   j
  //   R0
  //   R1
  //   R2
  //   R3
  //   j
  //   guess[0]
  //   guess[1]
  //   guess[2]
  //   guess[3]
  //   target[0]
  //   target[1]
  //   target[2]
  //   target[3]
  //   j (2 Bit Splitter)
  //   (j==4)
  //   j
  //   i
  //   flag[0]
  //   flag[1]
  //   flag[2]
  //   flag[3]
  //   Select Bit
  //   j (2 Bit)
  //   guess[j]
  //   target[j]
  //   Select Bit
  //   j (2 Bit)
  //   i+1
  //   guess[j]==target[j]
  //   RLED++
  //   i
  //   Select Bit
  //   i (2 Bit)
  //   Select Bit
  //   j (2 Bit)
  //   guess[0]
  //   guess[1]
  //   guess[2]
  //   guess[3]
  //   target[0]
  //   target[1]
  //   target[2]
  //   target[3]
  //   i (2 Bit Splitter)
  //   (i==4)
  //   flag[i]
  //   flag[i]==0
  //   flag[j]
  //   flag[j]==0
  //   Select Bit
  //   j (2 Bit)
  //   Select Bit
  //   i (2 Bit)
  //   guess[j]
  //   target[i]
  //   guess[j]!=target[i]
  //   WLED++
  //   WLed+1
  //   WLed
  //   RLed+1
  //   RLed
endmodule
