// Logisim project Simulate.circ as structural Verilog: 1 circuit, main circuit main
module main (
  input  go_i,
  input  [2:0] in0,
  input  [2:0] in1,
  input  [2:0] in2,
  input  [2:0] in3,
  output [2:0] RED,
  output [2:0] WHITE
);

  wire and_1_out, and_2_out, and_3_out, and_4_out, and_5_out, and_6_out, and_7_out, and_8_out, Clock_out,
       main_1_lflag, main_1_lg, main_1_li, main_1_lj, main_1_lred, main_1_lt, main_1_lwht, main_1_reset,
       main_1_si, main_1_sj, main_1_sjiadder, main_1_sred, main_1_swht, main_1_swradder, main_2_eflgi,
       main_2_eflgj, main_2_egtred, main_2_egtwht, main_2_ei, main_2_ej, not_1_out, not_2_out, not_3_out,
       not_4_out, not_5_out, not_6_out, or_1_out, or_2_out, or_3_out, or_4_out, or_5_out, or_6_out;

  Clock Clock (.out(Clock_out));
  ControlUnit_main main_1 (
    .go_i(go_i), .Clock(Clock_out), .Ei(main_2_ei), .Ej(main_2_ej), .Eflgi(main_2_eflgi),
    .Eflgj(main_2_eflgj), .EgtWht(main_2_egtwht), .EgtRed(main_2_egtred), .Lred(main_1_lred),
    .Lwht(main_1_lwht), .Reset(main_1_reset), .Lt(main_1_lt), .Lg(main_1_lg), .Lj(main_1_lj), .Sj(main_1_sj),
    .Lflag(main_1_lflag), .Sred(main_1_sred), .Swht(main_1_swht), .SwrAdder(main_1_swradder), .Li(main_1_li),
    .Si(main_1_si), .SjiAdder(main_1_sjiadder));
  Datapath_main main_2 (
    .Lg(main_1_lg), .in0(in0), .in1(in1), .in2(in2), .in3(in3), .Lt(main_1_lt), .Sj(main_1_sj),
    .Si(main_1_si), .Swht(main_1_swht), .Sred(main_1_sred), .Lj(main_1_lj), .Li(main_1_li),
    .Lwht(main_1_lwht), .Lred(main_1_lred), .Lflag(main_1_lflag), .Clock(Clock_out), .Reset(main_1_reset),
    .SjiAdder(main_1_sjiadder), .SwrAdder(main_1_swradder), .EgtRed(main_2_egtred), .EgtWht(main_2_egtwht),
    .RED(RED), .WHITE(WHITE), .Ej(main_2_ej), .Ei(main_2_ei), .Eflgi(main_2_eflgi), .Eflgj(main_2_eflgj));
  and and_1 (and_1_out, RED[1], RED[0], not_1_out);
  and and_2 (and_2_out, RED[2], not_3_out, not_2_out);
  or or_1 (or_1_out, and_2_out, and_1_out);
  LED led_1 (.in(or_1_out));
  LED led_2 (.in(and_2_out));
  not not_1 (not_1_out, RED[2]);
  not not_2 (not_2_out, RED[0]);
  not not_3 (not_3_out, RED[1]);
  and and_3 (and_3_out, not_1_out, not_3_out, RED[0]);
  and and_4 (and_4_out, not_1_out, RED[1], not_2_out);
  or or_2 (or_2_out, or_1_out, and_4_out);
  or or_3 (or_3_out, or_2_out, and_3_out);
  LED led_3 (.in(or_3_out));
  LED led_4 (.in(or_2_out));
  and and_5 (and_5_out, WHITE[2], not_6_out, not_5_out);
  or or_4 (or_4_out, and_5_out, and_8_out);
  LED led_5 (.in(and_5_out));
  not not_4 (not_4_out, WHITE[2]);
  not not_5 (not_5_out, WHITE[0]);
  not not_6 (not_6_out, WHITE[1]);
  and and_6 (and_6_out, not_4_out, not_6_out, WHITE[0]);
  and and_7 (and_7_out, not_4_out, WHITE[1], not_5_out);
  and and_8 (and_8_out, WHITE[1], WHITE[0], not_4_out);
  or or_5 (or_5_out, or_4_out, and_7_out);
  or or_6 (or_6_out, or_5_out, and_6_out);
  LED led_6 (.in(or_5_out));
  LED led_7 (.in(or_6_out));
  LED led_8 (.in(or_4_out));
endmodule
